// Logisim project additionneur-complet.circ as structural Verilog: 1 circuit, main circuit main
module main (
  input  a1,
  input  b1,
  input  r0,
  output out_4,
  output out_5
);

  wire and_1_out, and_2_out, xor_1_out;

  xor xor_1 (xor_1_out, b1, r0);
  and and_1 (and_1_out, b1, r0);
  and and_2 (and_2_out, a1, xor_1_out);
  xor xor_2 (out_4, a1, xor_1_out);
  or or_1 (out_5, and_2_out, and_1_out);
endmodule
